# Fritzing sketch 2048 (saved by Fritzing 0.9.3b)
breadboards: 1

parts:
  Часть1 = Arduino Nano (Rev3.0)
  S1 = Pushbutton [package="[THT]"]
  S2 = Pushbutton [package="[THT]"]
  S3 = Pushbutton [package="[THT]"]
  S4 = Pushbutton [package="[THT]"]
  S5 = Pushbutton [package="[THT]"]
  Grove1 = Grove OLED 128x96
  R1 = Resistor [tolerance=±5% resistance=10k package=THT]
  R2 = Resistor [tolerance=±5% resistance=10k package=THT]
  R3 = Resistor [tolerance=±5% resistance=10k package=THT]
  R4 = Resistor [tolerance=±5% resistance=10k package=THT]

nets:
  N1: Часть1.RESET, S5.Pin_2
  GND: Часть1.GND, S5.Pin_4, Grove1.GND, R1.Pin_1, R2.Pin_1, R3.Pin_1, R4.Pin_1
  N2: Часть1.D6, S4.Pin_1, S4.Pin_2, R4.Pin_0
  N3: Часть1.D7, S3.Pin_1, S3.Pin_2, R3.Pin_0
  N4: Часть1.D8, S2.Pin_1, S2.Pin_2, R2.Pin_0
  N5: Часть1.D9, S1.Pin_1, S1.Pin_2, R1.Pin_0
  5V: Часть1.5V, S1.Pin_3, S1.Pin_4, S2.Pin_3, S2.Pin_4, S3.Pin_3, S3.Pin_4, S4.Pin_3, S4.Pin_4, Grove1.VCC
  N6: Часть1.A5, Grove1.SCL
  N7: Часть1.A4, Grove1.SDA
